# Fritzing sketch without 220 (saved by Fritzing 0.9.4)
breadboards: 1

parts:
  S1 = Pushbutton [package="[THT]"]
  LED1 = LED - 5mm [color="Green (565nm)" package="5 mm [THT]"]
  R1 = Resistor [tolerance=±5% resistance=220 package=THT]
  Part1 = Arduino Uno (Rev3)

nets:
  N1: S1.Pin_1, S1.Pin_2, Part1.D4
  N2: S1.Pin_3, S1.Pin_4, R1.Pin_0, Part1.GND
  N3: LED1.cathode, R1.Pin_1
  N4: LED1.anode, Part1.D2
